# Fritzing sketch Wiring diagram (saved by Fritzing 0.9.5d)

parts:
  U1 = ESP8266 NodeMCU LoLin module
  Part1 = InvenSense MPU6050
  J1 = Piezo Speaker
  SG1 = Buzzer 12mm [package=buzzer-ccv-kit]  # not connected
  A1 = NEO-6M GPS Module [part_number=GY-GPS6MV2]
  HC-SR04_Sensor_1 = HC-SR04 Ultrasonic Distance Sensor

nets:
  N1: U1.D1, Part1.SCL
  N2: U1.D2, Part1.SDA
  N3: U1.D3, J1.pin2
  VCC: U1.3V3, Part1.VCC, A1.Vcc, HC-SR04_Sensor_1.VCC
  GND: U1.GND, Part1.GND, J1.pin1, A1.GND, HC-SR04_Sensor_1.GND
  N4: U1.D5, A1.Rx
  N5: U1.D6, A1.Tx
  N6: U1.D7, HC-SR04_Sensor_1.TRIG
  N7: U1.D8, HC-SR04_Sensor_1.ECHO

notes:
  GPS Neo 6M
  Buzzer
  Sensor Ultrasonik
  Sensor Kemiringan
  ESP8266

custom parts:
  ESP8266 NodeMCU LoLin module: ESP8266 based NodeMCU
  NEO-6M GPS Module: GY-GPS6MV2 NEO-6M GPS Module Module based on U-blox NEO-6M GPS engine, incorporating regulator for 3.3-5V DC input, MS621FE-compatible rechargeable battery for backup and EEPROM for storing configuration settings. Links: NEO-6 series product information page NEO-6 Datasheet
